# Fritzing sketch servobtn (saved by Fritzing 0.9.10b)
breadboards: 1

parts:
  부품1 = Arduino Uno (Rev3)
  J1 = Basic Servo
  J2 = Basic Servo
  SparkFun_Qwiic_6DoF_LSM6DSO1 = SparkFun Qwiic 6DoF LSM6DSO  # not connected
  R1 = Resistor [tolerance=±5% power=0.25 resistance=10k package=THT]
  S1 = Pushbutton [package="[THT]"]

nets:
  N1: 부품1.D9_PWM, J1.pulse
  N2: 부품1.D10_PWM/SS, J2.pulse
  N3: 부품1.D4, R1.Pin_1, S1.Pin_1, S1.Pin_2
  VCC: 부품1.5V, J1.vcc, J2.vcc, R1.Pin_0
  GND: 부품1.GND, J1.gnd, J2.gnd, S1.Pin_3, S1.Pin_4

custom parts:
  SparkFun Qwiic 6DoF LSM6DSO: The SparkFun LSM6DSO 6 Degrees of Freedom Breakout is an accelerometer and gyroscope sensor with a giant 9kB FIFO buffer and embedded processing interrupt functions. Due to the capabilities and low cost of the LSM6DSO we've created this small breakout board just for you! Each LSM6DSO breakout has been designed to be super-flexible and can be configured specifically for many applications. With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
